# Fritzing sketch Esquema Alarme Simples (saved by Fritzing 0.9.3b)
breadboards: 1

parts:
  UNO = Arduino Uno (Rev3)
  RES_TRANS = Resistor [tolerance=±5% resistance=1k package=THT]
  2N2222a = NPN-Transistor [package="TO92 [THT]"]
  DIODO_PROTECAO = Rectifier Diode [part_number=1N4007 package="300 mil [THT]"]
  RES_PULL_UP_BOTAO = Resistor [tolerance=±5% resistance=10k package=THT]
  RES_SENSOR = Resistor [tolerance=±5% resistance=10k package=THT]
  POWER = LED - 5mm [color="Green (570nm)" package="5 mm [THT]"]
  ARM = LED - 5mm [color="Blue (470nm)" package="5 mm [THT]"]
  ALARM = LED - 5mm [color="Red (660nm)" package="5 mm [THT]"]
  RES_LED_1 = Resistor [tolerance=±5% resistance=220 package=THT]
  RES_LED_2 = Resistor [tolerance=±5% resistance=220 package=THT]
  RES_LED_3 = Resistor [tolerance=±5% resistance=220 package=THT]
  BOTAO_ARMAR = Pushbutton [package=THT]
  SENSOR_(SEMPRE_FECHADO) = Pushbutton [package=THT]
  SIRENE_12V = Loudspeaker
  RELE_SIRENE = CAR RELAY [part_number=12V package=THT]
  ENERGIA = DC Power [voltage=12V]
  FONTE = DC Power [voltage=12V]

nets:
  N1: UNO.D8, RES_LED_1.Pin_0
  N2: UNO.D2, RES_SENSOR.Pin_0
  N3: UNO.D4, RES_PULL_UP_BOTAO.Pin_0
  N4: UNO.D5_PWM, RES_TRANS.Pin_0
  N5: UNO.D6_PWM, RES_LED_3.Pin_0
  N6: UNO.D7, RES_LED_2.Pin_0
  N7: UNO.5V, 2N2222a.C, DIODO_PROTECAO.cathode, DIODO_PROTECAO.anode, RELE_SIRENE.85
  N8: UNO.VIN, ENERGIA.V+
  N9: RES_TRANS.Pin_1, 2N2222a.B
  GND: 2N2222a.E, POWER.cathode, ARM.cathode, ALARM.cathode, BOTAO_ARMAR.leg0, SENSOR_(SEMPRE_FECHADO).leg0, RELE_SIRENE.86
  N10: RES_PULL_UP_BOTAO.Pin_1, BOTAO_ARMAR.leg1
  N11: RES_SENSOR.Pin_1, SENSOR_(SEMPRE_FECHADO).leg1
  N12: POWER.anode, RES_LED_2.Pin_1
  N13: ARM.anode, RES_LED_3.Pin_1
  N14: ALARM.anode, RES_LED_1.Pin_1
  N15: SIRENE_12V.pin1, RELE_SIRENE.30
  N16: SIRENE_12V.pin2, FONTE.V-
  N17: RELE_SIRENE.87, FONTE.V+

notes:
  Utilizei um botão como sensor acionador do alarme pois o funcionamento é igual ao de um botão que fica sempre fechado e abre ao ser acionado.
  UNO
  Anotei a origem do ground (UNO) somente para lembrar como montei na protoboard
